# Fritzing sketch CircuitoLuci_01 (saved by Fritzing 0.8.7b)
breadboards: 1

parts:
  Mosfet = Basic FET P-Channel [package="TO220 [THT]"]  # not connected
  Alimentazione_luci = Battery
  Arduino1 = Arduino Uno (Rev3)

nets:
  N1: Alimentazione_luci.-, Arduino1.GND

notes:
  Blocco luci alimentate a batteria
