# Fritzing sketch CircuitoLuci_01 (saved by Fritzing 0.9.1b)
breadboards: 1

parts:
  Alimentazione_luci1 = Battery
  Raspberry_Pi1 = Raspberry Pi B rev2
  Mosfet1 = Basic FET P-Channel [package="TO220 [THT]"]

nets:
  N1: Alimentazione_luci1.-, Raspberry_Pi1.GND, Mosfet1.drain
  N2: Raspberry_Pi1.GPIO_27, Mosfet1.gate

notes:
  Blocco luci alimentate a batteria
